# Fritzing sketch nurseryman_wiring (saved by Fritzing 0.9.3b)
breadboards: 1

parts:
  micro-sd_card_reader = MicroSD Card Module
  Bauteil2 = Arduino Uno (Rev3)
  BMP180 = Barometric Pressure Sensor - BMP180 Breakout (GY-68)
  DHT22 = Humidity and Temperature Sensor RHT03
  step-down_converter = RioRand LM2596
  17HD4005 = Stepper Motor - Bipolar
  YL-69 = Soil Moisture Sensor
  end_switch_right = Momentary Switch [package=tactile-pth]
  L298N = L298 [package=multiwatt15]
  end_switch_left = Momentary Switch [package=tactile-pth]
  R1 = Resistor [tolerance=±5% resistance=100k package=THT]
  submersible_pump = DC Motor
  relay = RELAY [package=relay-jzc]

nets:
  GND: micro-sd_card_reader.GND, Bauteil2.GND, BMP180.GND, DHT22.GND_2, step-down_converter.Pin_3, YL-69.GND, R1.Pin_1, submersible_pump.pin_1, relay.MAIN
  VCC: micro-sd_card_reader.VCC, DHT22.Vcc, step-down_converter.Pin_2, YL-69.VCC, end_switch_right.1, end_switch_left.1, relay.NO
  N1: micro-sd_card_reader.MISO, Bauteil2.D6_PWM
  N2: micro-sd_card_reader.MOSI, Bauteil2.D7
  N3: micro-sd_card_reader.SCK, Bauteil2.D5_PWM
  N4: micro-sd_card_reader.CS, Bauteil2.D13/SCK
  N5: Bauteil2.A3, YL-69.SIG
  N6: Bauteil2.A4/SDA, BMP180.SDA
  N7: Bauteil2.A5/SCL, BMP180.SCL
  N8: Bauteil2.D8, L298N.IN1
  N9: Bauteil2.D9_PWM, L298N.IN2
  N10: Bauteil2.D10_PWM/SS, L298N.IN3
  N11: Bauteil2.D11_PWM/MOSI, L298N.IN4
  N12: Bauteil2.D12/MISO, relay.COIL1
  N13: Bauteil2.D3_PWM, end_switch_right.4, end_switch_left.4, R1.Pin_0
  N14: Bauteil2.D4, DHT22.Data-signal
  3V3: Bauteil2.3V3, BMP180.VCC
  N15: 17HD4005.A, L298N.OUT4
  N16: 17HD4005.C, L298N.OUT3
  N17: 17HD4005.B, L298N.OUT1
  N18: 17HD4005.D, L298N.OUT2
  N19: submersible_pump.pin_2, relay.NC
